# Fritzing sketch regulateur_four_CSO (saved by Fritzing 0.9.3b)
breadboards: 1

parts:
  U1 = LM124-324 Quad Opamp [package="DIP (Dual Inline)"]
  J1 = Screw terminal - 2 pins [package=THT]
  V1 = DC Power [voltage=5]
  R1 = Resistor [tolerance=±5% resistance=330 package=THT]
  R2 = Resistor [tolerance=±5% resistance=330 package=THT]
  R3 = Resistor [tolerance=±5% resistance=27k package=THT]
  R4 = Resistor [tolerance=±5% resistance=27k package=THT]
  Grove1 = Grove 4 Digit Display
  Grove2 = Grove 4 Digit Display
  Composant1 = Arduino Uno (Rev3) - ICSP
  U2 = RELAY-SOLIDSTATE [package=relay-s108t02]
  J2 = Screw terminal - 2 pins [package=THT]
  J3 = Screw terminal - 2 pins [package=THT]
  U3 = MAX6675 [package=so08]  # not connected

nets:
  N1: U1.1OUT, R4.Pin_1, Composant1.A0
  N2: U1.1IN-, R2.Pin_1, R4.Pin_0
  N3: U1.1IN+, R1.Pin_1, R3.Pin_1
  N4: U1.VCC+, V1.V+
  GND: U1.VCC-, V1.V-, R3.Pin_0, Grove1.GND, Grove2.GND
  N5: J1.pin1, R1.Pin_0
  N6: J1.pin2, R2.Pin_0
  VCC: Grove1.VCC, Grove2.VCC
  N7: Grove1.DIO, Composant1.D3_PWM
  N8: Grove1.CLK, Composant1.D4
  N9: Grove2.CLK, Composant1.D2
  N10: Composant1.GND, U2.-
  N11: Composant1.D6_PWM, U2.+
  N12: U2.T1, J2.pin2
  N13: U2.T2, J3.pin1

notes:
  Temp sensor
  Vsensor- (V2)
  Vsensor+ (V1)
  L Phase in
  L Phase out
  Oven
  Power (~230V)
  CLK
  D1
  D2
  Display 1 (Measure C°)
  Display 2  (Set point)
